// Logisim project s-mips.circ as structural Verilog: 24 circuits, main circuit S-MIPS Board
module S_MIPS_Board (
  input  DESHABILITAR_DISPATCHER,
  output halt
);

  wire button_1_out, CLK, CS, d_ff_1_q, LCLR, LoadRAM, LoadRAMOn, LW, R_R_W, R_W, ram_dispatcher_1_finished,
       RCS, Reset_out, RST, TTY_EN;
  wire [2:0] KDB;
  wire [3:0] LMask, Mask, ram_1_read_time, ram_1_write_time, RMask;
  wire [6:0] KDB_DATA, TTY_DATA;
  wire [15:0] Addr, LAddr, RAddr;
  wire [31:0] I0, I1, I2, I3, LData, ram_1_data_out_0, ram_1_data_out_1, ram_1_data_out_2, ram_1_data_out_3,
       RI0, RI1, RI2, RI3;

  TTY #(.rows(25), .cols(80)) tty_1 (.data(TTY_DATA), .clk(CLK), .we(TTY_EN), .clr(RST));
  not not_1 (LoadRAMOn, ram_dispatcher_1_finished);
  RAM_Dispatcher ram_dispatcher_1 (
    .WriteTime(ram_1_write_time), .Clock(CLK), .Data(LData), .Address(LAddr), .Mask(LMask),
    .Finished(ram_dispatcher_1_finished), .Write(LW), .CLR(LCLR));
  Keyboard #(.buflen(64)) keyboard_1 (.clk(CLK), .re(KDB[0]), .avail(KDB[2]), .data(KDB_DATA));  // open: clr
  RAM ram_1 (
    .Address(RAddr), .Data_Out_0(ram_1_data_out_0), .Data_Out_1(ram_1_data_out_1),
    .Data_Out_2(ram_1_data_out_2), .Data_Out_3(ram_1_data_out_3), .Data_In_0(RI0), .Data_In_1(RI1),
    .Data_In_2(RI2), .Data_In_3(RI3), .Mask(RMask), .nRead_Write(R_R_W), .Chip_Select(RCS),
    .Read_Time(ram_1_read_time), .Reset(button_1_out), .Write_Time(ram_1_write_time));
  Button button_1 (.out(button_1_out));
  D_Flip_Flop d_ff_1 (.clk(CLK), .D(1'b1), .Q(d_ff_1_q), .reset(Reset_out));  // open: Qn, preset, en
  Button Reset (.out(Reset_out));
  S_MIPS s_mips_1 (
    .Kbd_Enable(KDB[0]), .Address(Addr), .Kbd_Clear(KDB[1]), .Kbd_Available(KDB[2]), .RAM_In_0(I0),
    .Kbd_ASCII_Data(KDB_DATA), .RAM_In_1(I1), .TTY_Enable(TTY_EN), .RAM_In_2(I2), .RAM_In_3(I3),
    .TTY_ASCII_Data(TTY_DATA), .Reset(RST), .RAM_Out_0(ram_1_data_out_0), .Clock(CLK),
    .RAM_Out_1(ram_1_data_out_1), .Stop(halt), .RAM_Out_2(ram_1_data_out_2), .RAM_Out_3(ram_1_data_out_3),
    .Mask(Mask), .Read_Time(ram_1_read_time), .Write_Time(ram_1_write_time), .nRead_Write(R_W),
    .Chip_Select(CS));
  D_Flip_Flop d_ff_2 (.clk(CLK), .D(d_ff_1_q), .Qn(LCLR), .reset(Reset_out));  // open: Q, preset, en
  or or_1 (RST, LCLR, LoadRAM);
  Clock clock_1 (.out(CLK));
  Multiplexer #(.width(32), .enable("false")) multiplexer_1 (.in0(I0), .in1(LData), .out(RI0), .sel(LoadRAM));
  Multiplexer #(.width(32), .enable("false")) multiplexer_2 (.in0(I1), .in1(LData), .out(RI1), .sel(LoadRAM));
  Multiplexer #(.width(32), .enable("false")) multiplexer_3 (.in0(I2), .in1(LData), .out(RI2), .sel(LoadRAM));
  Multiplexer #(.width(32), .enable("false")) multiplexer_4 (.in0(I3), .in1(LData), .out(RI3), .sel(LoadRAM));
  and and_1 (LoadRAM, ~DESHABILITAR_DISPATCHER, LoadRAMOn);  // AND_Gate
  Multiplexer #(.width(16), .enable("false")) multiplexer_5 (.in0(Addr), .in1(LAddr), .out(RAddr), .sel(LoadRAM));
  Multiplexer #(.width(4), .enable("false")) multiplexer_6 (.in0(Mask), .in1(LMask), .out(RMask), .sel(LoadRAM));
  Multiplexer #(.enable("false")) multiplexer_7 (.in0(CS), .in1(LW), .out(RCS), .sel(LoadRAM));
  Multiplexer #(.enable("false")) multiplexer_8 (.in0(R_W), .in1(LW), .out(R_R_W), .sel(LoadRAM));

  // Notes on the sheet:
  //   NO MODIFICAR
  //   Keyboard
endmodule

module RAM (
  input  [15:0] Address,
  input  [31:0] Data_In_0,
  input  [31:0] Data_In_1,
  input  [31:0] Data_In_2,
  input  [31:0] Data_In_3,
  input  [3:0] Mask,
  input  nRead_Write,
  input  Chip_Select,
  input  Reset,
  output [31:0] Data_Out_0,
  output [31:0] Data_Out_1,
  output [31:0] Data_Out_2,
  output [31:0] Data_Out_3,
  output [3:0] Read_Time,
  output [3:0] Write_Time
);

  wire and_2_out, and_3_out, and_4_out, and_5_out, and_6_out, and_7_out, and_8_out, and_9_out, Changed, CLK,
       comparator_2_eq, comparator_3_eq, comparator_4_eq, comparator_5_eq, comparator_6_eq, Count,
       demultiplexer_3_out0, Idle, Idle_q, Load, Load0, Load1, nand_1_out, or_1_out, or_2_out, or_3_out,
       or_4_out, or_5_out, or_6_out, or_7_out, or_8_out, or_9_out, or_10_out, Proc_q, Update_Mem, Zero_Time;
  wire [3:0] counter_1_q, multiplexer_1_out, subtractor_1_out;
  wire [31:0] register_1_q, register_2_q, register_3_q, register_4_q, register_5_q;

  // Probe on 4'b0011
  // Probe on 4'b0010
  Multiplexer #(.width(4), .enable("false")) multiplexer_1 (
    .in0(4'b0011), .in1(4'b0010), .out(multiplexer_1_out), .sel(nRead_Write));
  or or_1 (or_1_out, Idle, Update_Mem);
  or or_2 (or_2_out, ~Chip_Select, Reset);  // OR_Gate
  Subtractor #(.width(4)) subtractor_1 (.a(multiplexer_1_out), .b(4'b0010), .out(subtractor_1_out));  // open: bin, bout
  Demultiplexer #(.enable("false")) demultiplexer_1 (.out0(Idle), .out1(Load0), .in(Idle_q), .sel(Changed));
  D_Flip_Flop u_Idle (.clk(CLK), .D(or_1_out), .Q(Idle_q), .preset(or_2_out));  // open: Qn, en, reset
  // Probe on counter_1_q
  Counter #(.width(4), .max('hf)) counter_1 (
    .load(Load), .D(subtractor_1_out), .count(Count), .Q(counter_1_q), .clk(CLK), .clr(or_3_out));  // open: carry
  or or_3 (or_3_out, ~Chip_Select, Reset);  // OR_Gate
  Comparator_part #(.width(4), .mode("unsigned")) comparator_1 (
    .a(4'b0000), .b(counter_1_q), .eq(Zero_Time));  // open: gt, lt
  or or_4 (or_4_out, Count, Load0, Load1);
  Register #(.width(32)) register_1 (.D(Data_In_0), .en(Chip_Select), .Q(register_1_q), .clk(CLK), .clr(or_5_out));
  or or_5 (or_5_out, ~Chip_Select, Reset);  // OR_Gate
  Register #(.width(32)) register_2 (.D(Data_In_1), .en(Chip_Select), .Q(register_2_q), .clk(CLK), .clr(or_6_out));
  or or_6 (or_6_out, ~Chip_Select, Reset);  // OR_Gate
  Register #(.width(32)) register_3 (.D(Data_In_2), .en(Chip_Select), .Q(register_3_q), .clk(CLK), .clr(or_7_out));
  or or_7 (or_7_out, ~Chip_Select, Reset);  // OR_Gate
  Register #(.width(32)) register_4 (.D(Data_In_3), .en(Chip_Select), .Q(register_4_q), .clk(CLK), .clr(or_8_out));
  or or_8 (or_8_out, ~Chip_Select, Reset);  // OR_Gate
  Register #(.width(32)) register_5 (
    .D({{11{1'b1}}, nRead_Write, Mask, Address}), .en(Chip_Select), .Q(register_5_q), .clk(CLK),
    .clr(or_9_out));
  or or_9 (or_9_out, ~Chip_Select, Reset);  // OR_Gate
  D_Flip_Flop Proc (.clk(CLK), .D(or_4_out), .Q(Proc_q), .reset(or_10_out));  // open: Qn, preset, en
  or or_10 (or_10_out, ~Chip_Select, Reset);  // OR_Gate
  Demultiplexer #(.enable("false")) demultiplexer_2 (
    .out0(Count), .out1(Update_Mem), .in(demultiplexer_3_out0), .sel(Zero_Time));
  Demultiplexer #(.enable("false")) demultiplexer_3 (
    .out0(demultiplexer_3_out0), .out1(Load1), .in(Proc_q), .sel(Changed));
  Clock clock_1 (.out(CLK));
  Comparator_part #(.width(32)) comparator_2 (.a(register_1_q), .b(Data_In_0), .eq(comparator_2_eq));  // open: gt, lt
  Comparator_part #(.width(32)) comparator_3 (.a(register_2_q), .b(Data_In_1), .eq(comparator_3_eq));  // open: gt, lt
  Comparator_part #(.width(32)) comparator_4 (.a(register_3_q), .b(Data_In_2), .eq(comparator_4_eq));  // open: gt, lt
  Comparator_part #(.width(32)) comparator_5 (.a(register_4_q), .b(Data_In_3), .eq(comparator_5_eq));  // open: gt, lt
  Comparator_part #(.width(32)) comparator_6 (
    .a(register_5_q), .b({{11{1'b1}}, nRead_Write, Mask, Address}), .eq(comparator_6_eq));  // open: gt, lt
  nand nand_1 (nand_1_out, comparator_6_eq, comparator_2_eq, comparator_3_eq, comparator_4_eq, comparator_5_eq);
  and and_1 (Changed, nand_1_out, Chip_Select);
  or or_11 (Load, Count, Load1, Load0);
  and and_2 (and_2_out, Mask[0], Update_Mem, nRead_Write);
  and and_3 (and_3_out, Mask[1], Update_Mem, nRead_Write);
  and and_4 (and_4_out, Mask[2], Update_Mem, nRead_Write);
  and and_5 (and_5_out, Mask[3], Update_Mem, nRead_Write);
  RAM_part #(.addrWidth(16), .dataWidth(32), .bus("separate")) ram_1 (
    .addr(Address), .din(Data_In_0), .data(Data_Out_0), .str(and_2_out), .sel(Chip_Select), .clk(CLK),
    .ld(and_6_out), .clr(Reset));
  and and_6 (and_6_out, ~nRead_Write, Idle);  // AND_Gate
  RAM_part #(.addrWidth(16), .dataWidth(32), .bus("separate")) ram_2 (
    .addr(Address), .din(Data_In_1), .data(Data_Out_1), .str(and_3_out), .sel(Chip_Select), .clk(CLK),
    .ld(and_7_out), .clr(Reset));
  and and_7 (and_7_out, ~nRead_Write, Idle);  // AND_Gate
  RAM_part #(.addrWidth(16), .dataWidth(32), .bus("separate")) ram_3 (
    .addr(Address), .din(Data_In_2), .data(Data_Out_2), .str(and_4_out), .sel(Chip_Select), .clk(CLK),
    .ld(and_8_out), .clr(Reset));
  and and_8 (and_8_out, ~nRead_Write, Idle);  // AND_Gate
  RAM_part #(.addrWidth(16), .dataWidth(32), .bus("separate")) ram_4 (
    .addr(Address), .din(Data_In_3), .data(Data_Out_3), .str(and_5_out), .sel(Chip_Select), .clk(CLK),
    .ld(and_9_out), .clr(Reset));
  and and_9 (and_9_out, ~nRead_Write, Idle);  // AND_Gate

  assign Read_Time = 4'b0011;
  assign Write_Time = 4'b0010;

  // Other names for the same wires on the sheet: M0 = Mask[0]; M1 = Mask[1]; M2 = Mask[2]; M3 = Mask[3];
  //   RW = nRead_Write; CLR = Reset; CS = Chip_Select; Load2 = Count

  // Notes on the sheet:
  //   NO MODIFICAR
  //   excepto quizás los valores RT y WT
  //   BANK0
  //   BANK1
  //   BANK2
  //   BANK3
endmodule

module S_MIPS (
  input  Kbd_Available,
  input  [6:0] Kbd_ASCII_Data,
  input  [31:0] RAM_Out_0,
  input  [31:0] RAM_Out_1,
  input  Reset,
  input  [31:0] RAM_Out_2,
  input  Clock,
  input  [31:0] RAM_Out_3,
  input  [3:0] Read_Time,
  input  [3:0] Write_Time,
  output Kbd_Enable,
  output [15:0] Address,
  output Kbd_Clear,
  output TTY_Enable,
  output [6:0] TTY_ASCII_Data,
  output Stop,
  output [31:0] RAM_In_0,
  output [31:0] RAM_In_1,
  output [31:0] RAM_In_2,
  output [31:0] RAM_In_3,
  output [3:0] Mask,
  output nRead_Write,
  output Chip_Select
);

  wire AluInst, d_ff_1_q, enGI, enPC, enRF, getData, getIsnt, Halt, JmpInst, MemInst, or_1_out, or_2_out,
       ReadyData, ReadyInst, ReadyW, RInst, StackInst, Start, Tty, Write, WriteInst;
  wire [31:0] Address_t, DataIn, datapath_1_rout, multiplexer_1_out, multiplexer_2_out, multiplexer_3_out,
       multiplexer_4_out, ram_interaction_1_out_14, ram_interaction_1_out_15, ram_interaction_1_out_16,
       ram_interaction_1_out_17;

  D_Flip_Flop #(.trigger("falling")) d_ff_1 (
    .clk(Clock), .D(getIsnt), .Q(d_ff_1_q), .en(or_1_out));  // open: Qn, preset, reset
  or or_1 (or_1_out, getIsnt, ReadyInst);
  Multiplexer #(.width(32)) multiplexer_1 (
    .in0(RAM_Out_0), .in1(RAM_In_0), .out(multiplexer_1_out), .sel(Write));  // open: en
  Multiplexer #(.width(32)) multiplexer_2 (
    .in0(RAM_Out_1), .in1(RAM_In_0), .out(multiplexer_2_out), .sel(Write));  // open: en
  Multiplexer #(.width(32)) multiplexer_3 (
    .in0(RAM_Out_2), .in1(RAM_In_0), .out(multiplexer_3_out), .sel(Write));  // open: en
  Multiplexer #(.width(32)) multiplexer_4 (
    .in0(RAM_Out_3), .in1(RAM_In_0), .out(multiplexer_4_out), .sel(Write));  // open: en
  D_Flip_Flop #(.trigger("falling")) d_ff_2 (.clk(Clock), .D(Reset), .Q(Start));  // open: Qn, preset, en, reset
  DataPath datapath_1 (
    .in_1(DataIn), .in_2(Kbd_ASCII_Data), .in_3(Clock), .in_4(Reset), .in_5(d_ff_1_q), .out_10(Halt),
    .out_11(AluInst), .out_12(RInst), .out_13(JmpInst), .in_6(enGI), .in_7(enRF), .in_8(enPC),
    .in_9(Kbd_Available), .out_14(Tty), .out_15(MemInst), .out_16(StackInst), .out_17(WriteInst),
    .Output(Address_t), .ROut(datapath_1_rout), .TtyData(TTY_ASCII_Data));
  InOut inout_1 (.in_1(datapath_1_rout), .Output(RAM_In_0));
  RAM_Interaction ram_interaction_1 (
    .in_1(multiplexer_1_out), .in_2(multiplexer_2_out), .in_3(multiplexer_3_out), .in_4(multiplexer_4_out),
    .in_5(Address_t), .in_6(Read_Time), .in_7(Write_Time), .in_8(Clock), .in_9(Reset), .in_10(Write),
    .in_11(getIsnt), .in_12(getData), .in_13(enGI), .out_14(ram_interaction_1_out_14),
    .out_15(ram_interaction_1_out_15), .out_16(ram_interaction_1_out_16), .out_17(ram_interaction_1_out_17),
    .out_18(Address), .out_19(Mask), .out_20(nRead_Write), .out_21(Chip_Select), .out_22(ReadyInst),
    .out_23(ReadyData), .out_24(ReadyW));
  or or_2 (or_2_out, StackInst, MemInst);
  Multiplexer #(.select(2), .width(32)) multiplexer_5 (
    .in0(ram_interaction_1_out_14), .in1(ram_interaction_1_out_15), .in2(ram_interaction_1_out_16),
    .in3(ram_interaction_1_out_17), .out(DataIn), .sel(Address_t[3:2]));  // open: en
  Control_Unit control_unit_1 (
    .in_1(Clock), .in_2(Start), .in_3(ReadyInst), .in_4(AluInst), .in_5(RInst), .in_6(Reset), .in_7(Tty),
    .in_8(ReadyData), .in_9(JmpInst), .in_10(or_2_out), .in_11(WriteInst), .in_12(ReadyW), .out_13(enRF),
    .out_14(enPC), .out_15(Stop), .out_16(getData), .out_17(getIsnt), .out_18(enGI), .out_19(TTY_Enable),
    .out_20(Kbd_Enable), .out_21(Write));

  assign Kbd_Clear = Reset;
  assign RAM_In_1 = RAM_In_0;
  assign RAM_In_2 = RAM_In_0;
  assign RAM_In_3 = RAM_In_0;

  // Other names for the same wires on the sheet: CLK = Clock; CS = Chip_Select; KBD_AVAIL = Kbd_Available;
  //   CLR = Reset; KBD_CLR = Reset; KBD_DATA[6:0] = Kbd_ASCII_Data; RAM_A[15:0] = Address; RAM_MASK[3:0] = Mask;
  //   RAM_OUTPUT_0[31:0] = RAM_Out_0; RAM_OUTPUT_1[31:0] = RAM_Out_1; RAM_OUTPUT_2[31:0] = RAM_Out_2;
  //   RAM_OUTPUT_3[31:0] = RAM_Out_3; RAM_INPUT_0[31:0] = RAM_In_0; RAM_INPUT_1[31:0] = RAM_In_0;
  //   RAM_INPUT_2[31:0] = RAM_In_0; RAM_INPUT_3[31:0] = RAM_In_0; ROut[31:0] = RAM_In_0; RW = nRead_Write;
  //   TTY_DATA[6:0] = TTY_ASCII_Data

  // Notes on the sheet:
  //   RAM ADDRESS
  //   DATA FROM RAM
  //   DATA TO RAM
  //   DATA WRITE MASK
  //   RAM TIMING
  //   RAM CONTROL
  //   KEYBOARD
  //   TTY
  //   SEQUENCING
endmodule

module RAM_Dispatcher (
  input  [3:0] WriteTime,
  input  Clock,
  input  CLR,
  output [31:0] Data,
  output [15:0] Address,
  output [3:0] Mask,
  output Finished,
  output Write
);

  wire demultiplexer_2_out1, demultiplexer_3_out1, End, IDLE_q, IncAddr, Load, or_1_out, or_2_out, While_q,
       WriteEnd;
  wire [3:0] counter_1_q;
  wire [31:0] CurrentAddress_q;

  Counter #(.width(32), .max('hffffffff)) CurrentAddress (
    .count(IncAddr), .Q({CurrentAddress_q[31:18], Address, CurrentAddress_q[1:0]}), .clk(Clock), .clr(CLR));  // open: load, D, carry
  or or_1 (or_1_out, IncAddr, demultiplexer_3_out1, Finished);
  D_Flip_Flop IDLE (.clk(Clock), .D(or_1_out), .Q(IDLE_q), .preset(CLR));  // open: Qn, en, reset
  Demultiplexer #(.enable("false")) demultiplexer_1 (.out0(Load), .out1(Finished), .in(IDLE_q), .sel(End));
  D_Flip_Flop While (.clk(Clock), .D(or_2_out), .Q(While_q), .reset(CLR));  // open: Qn, preset, en
  or or_2 (or_2_out, Write, Load);
  RAM_part #(.addrWidth(18), .dataWidth(32)) ram_1 (
    .addr({Address, CurrentAddress_q[1:0]}), .data(Data), .clk(Clock));  // open: sel, ld, clr
  Demultiplexer #(.enable("false")) demultiplexer_2 (
    .out0(Write), .out1(demultiplexer_2_out1), .in(While_q), .sel(WriteEnd));
  Decoder #(.select(2)) decoder_1 (
    .out0(Mask[0]), .out1(Mask[1]), .out2(Mask[2]), .out3(Mask[3]), .sel(CurrentAddress_q[1:0]));  // open: en
  Demultiplexer #(.enable("false")) demultiplexer_3 (
    .out0(IncAddr), .out1(demultiplexer_3_out1), .in(demultiplexer_2_out1), .sel(End));
  Counter #(.width(4), .max('hf)) counter_1 (
    .load(Load), .D(WriteTime), .count(Write), .Q(counter_1_q), .clk(Clock));  // open: carry, clr
  Comparator_part #(.width(32)) comparator_1 (.a(Data), .b({32{1'b1}}), .eq(End));  // open: gt, lt
  Comparator_part #(.width(4)) comparator_2 (.a(4'b0000), .b(counter_1_q), .eq(WriteEnd));  // open: gt, lt

  // Other names for the same wires on the sheet: CLK = Clock; Count = Write; WT[3:0] = WriteTime
endmodule

module TipoR (
  input  [5:0] in_1,
  input  in_2,
  input  in_3,
  input  in_4,
  output Output,
  output Output_2,
  output Output_3,
  output Output_4,
  output Output_5,
  output Output_6,
  output Output_7,
  output Output_8,
  output Output_9,
  output Output_10,
  output Output_11,
  output Output_12,
  output Output_13,
  output Output_14,
  output Output_15,
  output Output_16,
  output Output_17,
  output Output_18,
  output Output_19,
  output Output_20,
  output Output_21,
  output Output_22
);

  wire and_1_out, and_2_out, and_3_out, and_11_out, and_12_out, and_13_out, and_20_out, and_21_out,
       and_22_out, and_23_out, and_24_out, and_25_out;

  and and_1 (and_1_out, ~in_1[1], ~in_1[2], ~in_1[3], ~in_1[4], ~in_1[5]);  // AND_Gate
  and and_2 (and_2_out, ~in_1[0], ~in_1[2], ~in_1[3], ~in_1[4], in_1[5]);  // AND_Gate
  and and_3 (and_3_out, ~in_1[1], ~in_1[2], in_1[3], in_1[4], ~in_1[5]);  // AND_Gate
  and and_4 (Output, and_1_out, in_2);
  and and_5 (Output_2, and_1_out, ~in_1[0], in_3);  // AND_Gate
  and and_6 (Output_3, and_1_out, in_1[0], in_3);
  and and_7 (Output_5, and_2_out, ~in_1[1], in_2);  // AND_Gate
  and and_8 (Output_8, and_2_out, in_1[1], in_2);
  and and_9 (Output_11, and_3_out, ~in_1[0], in_2);  // AND_Gate
  and and_10 (Output_14, in_2, in_1[0], and_3_out);
  and and_11 (and_11_out, in_1[1], ~in_1[2], in_1[3], in_1[4], ~in_1[5]);  // AND_Gate
  and and_12 (and_12_out, in_1[1], ~in_1[2], in_1[3], ~in_1[4], in_1[5]);  // AND_Gate
  and and_13 (and_13_out, ~in_1[1], in_1[2], ~in_1[3], ~in_1[4], in_1[5]);  // AND_Gate
  and and_14 (Output_17, and_11_out, ~in_1[0], in_2);  // AND_Gate
  and and_15 (Output_20, and_11_out, in_1[0], in_2);
  and and_16 (Output_6, and_12_out, ~in_1[0], in_2);  // AND_Gate
  and and_17 (Output_9, and_12_out, in_1[0], in_2);
  and and_18 (Output_12, and_13_out, ~in_1[0], in_2);  // AND_Gate
  and and_19 (Output_15, and_13_out, in_1[0], in_2);
  and and_20 (and_20_out, ~in_1[3], ~in_1[4], ~in_1[5]);  // AND_Gate
  and and_21 (and_21_out, in_1[0], in_1[1], in_1[2], ~in_1[3], ~in_1[4], in_1[5]);  // AND_Gate
  and and_22 (and_22_out, ~in_1[0], ~in_1[1], ~in_1[2], in_1[3], ~in_1[4], in_1[5]);  // AND_Gate
  and and_23 (and_23_out, ~in_1[0], ~in_1[1], ~in_1[2], in_1[3], ~in_1[4], ~in_1[5]);  // AND_Gate
  and and_24 (and_24_out, ~in_1[0], ~in_1[2], ~in_1[3], in_1[4], ~in_1[5]);  // AND_Gate
  and and_25 (and_25_out, in_1[0], in_1[1], in_1[2], in_1[3], in_1[4], in_1[5]);
  and and_26 (Output_19, and_20_out, in_1[0], in_4);
  and and_27 (Output_22, and_20_out, in_1[1], in_4);
  and and_28 (Output_4, and_20_out, in_1[2], in_4);
  and and_29 (Output_18, and_21_out, in_2);
  and and_30 (Output_21, and_22_out, in_2);
  and and_31 (Output_7, and_23_out, in_2);
  and and_32 (Output_10, and_24_out, ~in_1[1], in_2);  // AND_Gate
  and and_33 (Output_13, and_24_out, in_1[1], in_2);
  and and_34 (Output_16, and_25_out, in_4);

  // Other names for the same wires on the sheet: _000000 = in_2; _111000 = in_3; _111111 = in_4; add = Output_5;
  //   and = Output_12; div = Output_17; divu = Output_20; func_code[5:0] = in_1; halt = Output_16; jr = Output_7;
  //   kbd = Output_4; mfhi = Output_10; mflo = Output_13; mult = Output_11; mulu = Output_14; nop = Output;
  //   nor = Output_18; or = Output_15; pop = Output_2; push = Output_3; rnd = Output_22; slt = Output_6;
  //   sltu = Output_9; sub = Output_8; tty = Output_19; xor = Output_21

  // Notes on the sheet:
  //   add-sub
  //   mult-mulu
  //   nop-pop-push
  //   div-divu
  //   slt-sltu
  //   and-or
  //   tty-rnd-kbd
  //   jr
  //   nor
  //   xor
  //   mfhi-mflo
  //   halt
endmodule

module TipoI (
  input  [5:0] in_1,
  output Output,
  output Output_2,
  output Output_3,
  output Output_4,
  output Output_5,
  output Output_6,
  output Output_7,
  output Output_8,
  output Output_9,
  output Output_10,
  output Output_11,
  output Output_12,
  output Output_13
);

  and and_1 (Output, ~in_1[0], ~in_1[1], ~in_1[2], in_1[3], ~in_1[4], ~in_1[5]);  // AND_Gate
  and and_2 (Output_5, ~in_1[0], in_1[1], ~in_1[2], in_1[3], ~in_1[4], ~in_1[5]);  // AND_Gate
  and and_3 (Output_8, in_1[0], in_1[1], ~in_1[2], in_1[3], ~in_1[4], ~in_1[5]);  // AND_Gate
  and and_4 (Output_11, ~in_1[0], ~in_1[1], in_1[2], in_1[3], ~in_1[4], ~in_1[5]);  // AND_Gate
  and and_5 (Output_2, ~in_1[0], in_1[1], in_1[2], in_1[3], ~in_1[4], ~in_1[5]);  // AND_Gate
  and and_6 (Output_6, in_1[0], ~in_1[1], in_1[2], in_1[3], ~in_1[4], ~in_1[5]);  // AND_Gate
  and and_7 (Output_9, in_1[0], in_1[1], ~in_1[2], ~in_1[3], ~in_1[4], in_1[5]);  // AND_Gate
  and and_8 (Output_12, in_1[0], in_1[1], ~in_1[2], in_1[3], ~in_1[4], in_1[5]);  // AND_Gate
  and and_9 (Output_3, ~in_1[0], ~in_1[1], in_1[2], ~in_1[3], ~in_1[4], ~in_1[5]);  // AND_Gate
  and and_10 (Output_7, in_1[0], ~in_1[1], in_1[2], ~in_1[3], ~in_1[4], ~in_1[5]);  // AND_Gate
  and and_11 (Output_10, ~in_1[0], in_1[1], in_1[2], ~in_1[3], ~in_1[4], ~in_1[5]);  // AND_Gate
  and and_12 (Output_13, in_1[0], in_1[1], in_1[2], ~in_1[3], ~in_1[4], ~in_1[5]);  // AND_Gate
  and and_13 (Output_4, in_1[0], ~in_1[1], ~in_1[2], ~in_1[3], ~in_1[4], ~in_1[5]);  // AND_Gate

  // Other names for the same wires on the sheet: addi = Output; andi = Output_11; beq = Output_3; bgtz = Output_13;
  //   blez = Output_10; bltz = Output_4; bne = Output_7; lw = Output_9; op[5:0] = in_1; ori = Output_6;
  //   slti = Output_5; sltiu = Output_8; sw = Output_12; xori = Output_2

  // Notes on the sheet:
  //   addi
  //   slti
  //   sltiu
  //   andi
  //   xori
  //   ori
  //   load word
  //   store word
  //   beq
  //   bne
  //   blez
  //   bgtz
  //   bltz
endmodule

// Destino
module Instruction_Decoder (
  input  [31:0] in_1,
  output Output,
  output Output_2,
  output Output_3,
  output Output_4,
  output Output_5,
  output Output_6,
  output Output_7,
  output Output_8,
  output Output_9,
  output Output_10,
  output Output_11,
  output [4:0] Output_12,
  output Output_13,
  output Output_14,
  output Output_15,
  output Output_16,
  output Output_17,
  output [4:0] Output_18,
  output Output_19,
  output Output_20,
  output Output_21,
  output Output_22,
  output Output_23,
  output [4:0] Output_24,
  output Output_25,
  output Output_26,
  output Output_27,
  output Output_28,
  output Output_29,
  output [15:0] out_31,
  output Output_30,
  output Output_31,
  output Output_32,
  output Output_33,
  output Output_34,
  output Output_35,
  output Output_36,
  output Output_37,
  output Output_38,
  output Output_39,
  output [25:0] out_42
);

  wire _000000, _111000, _111111;

  and and_1 (_000000, ~in_1[26], ~in_1[27], ~in_1[28], ~in_1[29], ~in_1[30], ~in_1[31]);  // AND_Gate
  and and_2 (_111000, ~in_1[26], ~in_1[27], ~in_1[28], in_1[29], in_1[30], in_1[31]);  // AND_Gate
  and and_3 (_111111, in_1[26], in_1[27], in_1[28], in_1[29], in_1[30], in_1[31]);
  TipoR tipor_1 (
    .Output(Output), .Output_2(Output_2), .Output_3(Output_3), .Output_4(Output_4), .Output_5(Output_7),
    .Output_6(Output_8), .Output_7(Output_9), .in_1(in_1[5:0]), .Output_8(Output_13), .Output_9(Output_14),
    .Output_10(Output_15), .in_2(_000000), .Output_11(Output_19), .Output_12(Output_20),
    .Output_13(Output_21), .in_3(_111000), .Output_14(Output_25), .Output_15(Output_26),
    .Output_16(Output_27), .Output_17(Output_30), .Output_18(Output_31), .Output_19(Output_32),
    .in_4(_111111), .Output_20(Output_35), .Output_21(Output_36), .Output_22(Output_37));
  TipoI tipoi_1 (
    .Output(Output_10), .Output_2(Output_33), .Output_3(Output_17), .Output_4(Output_39),
    .Output_5(Output_16), .Output_6(Output_38), .Output_7(Output_23), .in_1(in_1[31:26]),
    .Output_8(Output_22), .Output_9(Output_5), .Output_10(Output_29), .Output_11(Output_28),
    .Output_12(Output_11), .Output_13(Output_34));
  and and_4 (Output_6, ~in_1[26], in_1[27], ~in_1[28], ~in_1[29], ~in_1[30], ~in_1[31]);  // AND_Gate

  assign out_31 = in_1[15:0];
  assign out_42 = in_1[25:0];
  assign Output_12 = in_1[25:21];
  assign Output_18 = in_1[20:16];
  assign Output_24 = in_1[15:11];

  // Other names for the same wires on the sheet: add = Output_7; addi = Output_10; and = Output_20; andi = Output_28;
  //   beq = Output_17; bgtz = Output_34; blez = Output_29; bltz = Output_39; bne = Output_23; div = Output_30;
  //   divu = Output_35; halt = Output_27; Constante[15:0] = in_1[15:0]; Destino[25:0] = in_1[25:0];
  //   FC[5:0] = in_1[5:0]; X[4:0] = in_1[10:6]; RD[4:0] = in_1[15:11]; RT[4:0] = in_1[20:16]; RS[4:0] = in_1[25:21];
  //   OP[5:0] = in_1[31:26]; J = Output_6; jr = Output_9; kbd = Output_4; lw = Output_5; mfhi = Output_15;
  //   mflo = Output_21; mult = Output_19; mulu = Output_25; nop = Output; nor = Output_31; or = Output_26;
  //   ori = Output_38; pop = Output_2; push = Output_3; rnd = Output_37; slt = Output_8; slti = Output_16;
  //   sltiu = Output_22; sltu = Output_14; sub = Output_13; sw = Output_11; tty = Output_32; xor = Output_36;
  //   xori = Output_33

  // Notes on the sheet:
  //   Instruction Decoder
endmodule

module Register_File (
  input  in_1,
  input  in_2,
  input  in_3,
  input  [4:0] in_4,
  input  [4:0] in_5,
  input  [31:0] in_6,
  input  [4:0] in_7,
  input  in_8,
  input  in_9,
  input  in_10,
  output [31:0] Output,
  output [31:0] Output_2,
  output [31:0] Output_3
);

  wire In31, L0, L1, L2, L3, L4, L5, L6, L7, L8, L9, L10, L11, L12, L13, L14, L15, L16, L17, L18, L19, L20,
       L21, L22, L23, L24, L25, L26, L27, L28, L29, L30, L31, or_1_out, or_2_out;
  wire [31:0] adder_1_out, multiplexer_3_out, multiplexer_4_out, multiplexer_5_out, Out0, Out1, Out2, Out3,
       Out4, Out5, Out6, Out7, Out8, Out9, Out10, Out11, Out12, Out13, Out14, Out15, Out16, Out17, Out18,
       Out19, Out20, Out21, Out22, Out23, Out24, Out25, Out26, Out27, Out28, Out29, Out30, subtractor_1_out;

  Register #(.width(32)) register_1 (.D({32{1'b0}}), .en(L0), .Q(Out0), .clk(in_2), .clr(in_1));
  Register #(.width(32)) register_2 (.D(in_6), .en(L8), .Q(Out8), .clk(in_2), .clr(in_1));
  Register #(.width(32)) register_3 (.D(in_6), .en(L16), .Q(Out16), .clk(in_2), .clr(in_1));
  Register #(.width(32)) register_4 (.D(in_6), .en(L24), .Q(Out24), .clk(in_2), .clr(in_1));
  Demultiplexer #(.select(5), .enable("false")) demultiplexer_1 (
    .out0(L0), .out1(L1), .out2(L2), .out3(L3), .out4(L4), .out5(L5), .out6(L6), .out7(L7), .out8(L8),
    .out9(L9), .out10(L10), .out11(L11), .out12(L12), .out13(L13), .out14(L14), .out15(L15), .out16(L16),
    .out17(L17), .out18(L18), .out19(L19), .out20(L20), .out21(L21), .out22(L22), .out23(L23), .out24(L24),
    .out25(L25), .out26(L26), .out27(L27), .out28(L28), .out29(L29), .out30(L30), .out31(In31), .in(in_3),
    .sel(in_4));
  Register #(.width(32)) register_5 (.D(in_6), .en(L1), .Q(Out1), .clk(in_2), .clr(in_1));
  Register #(.width(32)) register_6 (.D(in_6), .en(L9), .Q(Out9), .clk(in_2), .clr(in_1));
  Register #(.width(32)) register_7 (.D(in_6), .en(L17), .Q(Out17), .clk(in_2), .clr(in_1));
  Register #(.width(32)) register_8 (.D(in_6), .en(L25), .Q(Out25), .clk(in_2), .clr(in_1));
  Register #(.width(32)) register_9 (.D(in_6), .en(L2), .Q(Out2), .clk(in_2), .clr(in_1));
  Register #(.width(32)) register_10 (.D(in_6), .en(L10), .Q(Out10), .clk(in_2), .clr(in_1));
  Register #(.width(32)) register_11 (.D(in_6), .en(L18), .Q(Out18), .clk(in_2), .clr(in_1));
  Register #(.width(32)) register_12 (.D(in_6), .en(L26), .Q(Out26), .clk(in_2), .clr(in_1));
  Multiplexer #(.select(5), .width(32), .enable("false")) multiplexer_1 (
    .in0(Out0), .in1(Out1), .in2(Out2), .in3(Out3), .in4(Out4), .in5(Out5), .in6(Out6), .in7(Out7),
    .in8(Out8), .in9(Out9), .in10(Out10), .in11(Out11), .in12(Out12), .in13(Out13), .in14(Out14),
    .in15(Out15), .in16(Out16), .in17(Out17), .in18(Out18), .in19(Out19), .in20(Out20), .in21(Out21),
    .in22(Out22), .in23(Out23), .in24(Out24), .in25(Out25), .in26(Out26), .in27(Out27), .in28(Out28),
    .in29(Out29), .in30(Out30), .in31(Output_3), .out(Output), .sel(in_5));
  Register #(.width(32)) register_13 (.D(in_6), .en(L3), .Q(Out3), .clk(in_2), .clr(in_1));
  Register #(.width(32)) register_14 (.D(in_6), .en(L11), .Q(Out11), .clk(in_2), .clr(in_1));
  Register #(.width(32)) register_15 (.D(in_6), .en(L19), .Q(Out19), .clk(in_2), .clr(in_1));
  Register #(.width(32)) register_16 (.D(in_6), .en(L27), .Q(Out27), .clk(in_2), .clr(in_1));
  Register #(.width(32)) register_17 (.D(in_6), .en(L4), .Q(Out4), .clk(in_2), .clr(in_1));
  Register #(.width(32)) register_18 (.D(in_6), .en(L12), .Q(Out12), .clk(in_2), .clr(in_1));
  Register #(.width(32)) register_19 (.D(in_6), .en(L20), .Q(Out20), .clk(in_2), .clr(in_1));
  Register #(.width(32)) register_20 (.D(in_6), .en(L28), .Q(Out28), .clk(in_2), .clr(in_1));
  Multiplexer #(.select(5), .width(32), .enable("false")) multiplexer_2 (
    .in0(Out0), .in1(Out1), .in2(Out2), .in3(Out3), .in4(Out4), .in5(Out5), .in6(Out6), .in7(Out7),
    .in8(Out8), .in9(Out9), .in10(Out10), .in11(Out11), .in12(Out12), .in13(Out13), .in14(Out14),
    .in15(Out15), .in16(Out16), .in17(Out17), .in18(Out18), .in19(Out19), .in20(Out20), .in21(Out21),
    .in22(Out22), .in23(Out23), .in24(Out24), .in25(Out25), .in26(Out26), .in27(Out27), .in28(Out28),
    .in29(Out29), .in30(Out30), .in31(Output_3), .out(Output_2), .sel(in_7));
  Register #(.width(32)) register_21 (.D(in_6), .en(L5), .Q(Out5), .clk(in_2), .clr(in_1));
  Register #(.width(32)) register_22 (.D(in_6), .en(L13), .Q(Out13), .clk(in_2), .clr(in_1));
  Register #(.width(32)) register_23 (.D(in_6), .en(L21), .Q(Out21), .clk(in_2), .clr(in_1));
  Register #(.width(32)) register_24 (.D(in_6), .en(L29), .Q(Out29), .clk(in_2), .clr(in_1));
  Subtractor #(.width(32)) subtractor_1 (.a(Output_3), .b(32'h4), .out(subtractor_1_out));  // open: bin, bout
  Adder #(.width(32)) adder_1 (.a(32'h4), .b(Output_3), .out(adder_1_out));  // open: cin, cout
  Multiplexer #(.width(32), .enable("false")) multiplexer_3 (
    .in0(subtractor_1_out), .in1(adder_1_out), .out(multiplexer_3_out), .sel(in_8));
  Register #(.width(32)) register_25 (.D(in_6), .en(L6), .Q(Out6), .clk(in_2), .clr(in_1));
  Register #(.width(32)) register_26 (.D(in_6), .en(L14), .Q(Out14), .clk(in_2), .clr(in_1));
  Register #(.width(32)) register_27 (.D(in_6), .en(L22), .Q(Out22), .clk(in_2), .clr(in_1));
  Register #(.width(32)) register_28 (.D(in_6), .en(L30), .Q(Out30), .clk(in_2), .clr(in_1));
  Multiplexer #(.width(32), .enable("false")) multiplexer_4 (
    .in0(multiplexer_3_out), .in1({32{1'b1}}), .out(multiplexer_4_out), .sel(in_1));
  Register #(.width(32)) register_29 (.D(in_6), .en(L7), .Q(Out7), .clk(in_2), .clr(in_1));
  Register #(.width(32)) register_30 (.D(in_6), .en(L15), .Q(Out15), .clk(in_2), .clr(in_1));
  Register #(.width(32)) register_31 (.D(in_6), .en(L23), .Q(Out23), .clk(in_2), .clr(in_1));
  or or_1 (or_1_out, in_9, in_8);
  Multiplexer #(.width(32)) multiplexer_5 (
    .in0(multiplexer_4_out), .in1(in_6), .out(multiplexer_5_out), .sel(In31));  // open: en
  or or_2 (or_2_out, L31, In31, in_1);
  and and_1 (L31, in_10, or_1_out);
  Register #(.width(32)) register_32 (.D(multiplexer_5_out), .en(or_2_out), .Q(Output_3), .clk(in_2));  // open: clr

  // Other names for the same wires on the sheet: A[31:0] = Output; B[31:0] = Output_2; clk = in_2; Input[31:0] = in_6;
  //   MemRW = in_10; Out31[31:0] = Output_3; outA[4:0] = in_5; outB[4:0] = in_7; pop = in_8; push = in_9;
  //   reset = in_1; sel[4:0] = in_4; write = in_3
endmodule

module Get_Instruction (
  input  in_1,
  input  [31:0] in_2,
  input  in_3,
  input  in_4,
  output [31:0] out_5
);

  Register #(.width(32)) register_1 (
    .D(in_2), .en(in_4), .Q({out_5[7:0], out_5[15:8], out_5[23:16], out_5[31:24]}), .clk(in_1), .clr(in_3));

  // Other names for the same wires on the sheet: clk = in_1; enable = in_4; inst[31:0] = in_2; out[31:0] = out_5;
  //   reset = in_3
endmodule

module ALU (
  input  [31:0] in_1,
  input  [3:0] in_2,
  input  in_3,
  input  [31:0] in_4,
  input  in_5,
  input  in_6,
  output [31:0] Output,
  output [31:0] out_8,
  output [31:0] Output_2
);

  wire div, Enable, mult, or_2_out;
  wire [31:0] add, \and , Cocient, multiplexer_2_out, multiplexer_3_out, MultLower, MultUpper, \nor , \or ,
       Remainder, slt, sub, \xor ;

  Adder #(.width(32)) adder_1 (.a(in_1), .b(in_4), .out(add));  // open: cin, cout
  Subtractor #(.width(32)) subtractor_1 (.a(in_1), .b(in_4), .out(sub));  // open: bin, bout
  assign \and  = in_1 & in_4;  // AND_Gate and_1, 32 bits wide
  assign \or  = in_1 | in_4;  // OR_Gate or_1, 32 bits wide
  assign \nor  = ~(in_1 | in_4);  // NOR_Gate nor_1, 32 bits wide
  assign \xor  = in_1 ^ in_4;  // XOR_Gate xor_1, 32 bits wide
  Comparator comparator_1 (.in_1(in_1), .in_2(in_4), .in_3(in_6), .Output(slt));
  Multiplier multiplier_1 (.in_1(in_1), .in_2(in_4), .in_3(in_6), .Output(MultLower), .Output_2(MultUpper));
  Divider divider_1 (.in_1(in_1), .in_2(in_4), .in_3(in_6), .Output(Cocient), .Output_2(Remainder));
  Multiplexer #(.select(4), .width(32), .enable("false")) multiplexer_1 (
    .in1(add), .in2(sub), .in3(\and ), .in4(\or ), .in5(\nor ), .in6(\xor ), .in7(slt), .out(out_8),
    .sel(in_2));  // open: in0, in8, in9, in10, in11, in12, in13, in14, in15
  Comparator_part #(.width(4)) comparator_2 (.a(in_2), .b(4'b0000), .eq(mult));  // open: gt, lt
  Comparator_part #(.width(4)) comparator_3 (.a(in_2), .b(4'b1111), .eq(div));  // open: gt, lt
  or or_2 (or_2_out, mult, div);
  Multiplexer #(.width(32), .enable("false")) multiplexer_2 (
    .in0(MultLower), .in1(Cocient), .out(multiplexer_2_out), .sel(div));
  Register #(.width(32)) register_1 (.D(multiplexer_2_out), .en(Enable), .Q(Output), .clk(in_3));  // open: clr
  Register #(.width(32)) register_2 (.D(multiplexer_3_out), .en(Enable), .Q(Output_2), .clk(in_3));  // open: clr
  Multiplexer #(.width(32), .enable("false")) multiplexer_3 (
    .in0(MultUpper), .in1(Remainder), .out(multiplexer_3_out), .sel(div));
  and and_2 (Enable, or_2_out, in_5);

  // Other names for the same wires on the sheet: A[31:0] = in_1; B[31:0] = in_4; CLK = in_3; HI[31:0] = Output_2;
  //   LO[31:0] = Output; on = in_5; OpSel[3:0] = in_2; unsigned = in_6
endmodule

module Abs (
  input  [31:0] in_1,
  input  in_2,
  output [31:0] Output,
  output Output_2
);

  wire and_1_out;
  wire [31:0] negator_1_out;

  Multiplexer #(.width(32)) multiplexer_1 (.in0(in_1), .in1(negator_1_out), .out(Output), .sel(and_1_out));  // open: en
  Negator #(.width(32)) negator_1 (.in(in_1), .out(negator_1_out));
  and and_1 (and_1_out, in_1[31], ~in_2);  // AND_Gate

  assign Output_2 = in_1[31];

  // Other names for the same wires on the sheet: bit31 = in_1[31]; unsigned = in_2
endmodule

module Multiplier (
  input  [31:0] in_1,
  input  [31:0] in_2,
  input  in_3,
  output [31:0] Output,
  output [31:0] Output_2
);

  wire adder_1_cout, sel, sigA, sigB, xor_1_out;
  wire [31:0] absA, absB, bit_extender_1_out, HI, LO, not_1_out, not_2_out, SHI, SLO;

  Abs abs_1 (.in_1(in_1), .Output_2(sigA), .Output(absA), .in_2(in_3));
  Abs abs_2 (.in_1(in_2), .Output_2(sigB), .Output(absB), .in_2(in_3));
  Multiplier_part #(.width(32)) multiplier_1 (.a(absA), .b(absB), .out(LO), .cout(HI));  // open: cin
  and and_1 (sel, ~in_3, xor_1_out);  // AND_Gate
  xor xor_1 (xor_1_out, sigA, sigB);
  Multiplexer #(.width(32)) multiplexer_1 (.in0(LO), .in1(SLO), .out(Output), .sel(sel));  // open: en
  Multiplexer #(.width(32)) multiplexer_2 (.in0(HI), .in1(SHI), .out(Output_2), .sel(sel));  // open: en
  assign not_1_out = ~LO;  // NOT_Gate not_1, 32 bits wide
  Adder #(.width(32)) adder_1 (.a(not_1_out), .b(32'h1), .out(SLO), .cout(adder_1_cout));  // open: cin
  assign not_2_out = ~HI;  // NOT_Gate not_2, 32 bits wide
  assign bit_extender_1_out = {{31{1'b0}}, adder_1_cout};  // Bit_Extender bit_extender_1
  Adder #(.width(32)) adder_2 (.a(not_2_out), .b(bit_extender_1_out), .out(SHI));  // open: cin, cout

  // Other names for the same wires on the sheet: A[31:0] = in_1; B[31:0] = in_2; FHI[31:0] = Output_2;
  //   FLO[31:0] = Output; unsigned = in_3
endmodule

module Divider (
  input  [31:0] in_1,
  input  [31:0] in_2,
  input  in_3,
  output [31:0] Output,
  output [31:0] Output_2
);

  wire negA, negB, negO, sigA, sigB;
  wire [31:0] absA, absB, adder_1_out, divider_1_out, multiplexer_2_out, negator_1_out, R, subtractor_1_out;

  Abs abs_1 (.in_1(in_1), .Output_2(sigA), .Output(absA), .in_2(in_3));
  Divider_part #(.width(32)) divider_1 (.a(absA), .b(absB), .out(divider_1_out), .rem(R));  // open: upper
  Subtractor #(.width(32)) subtractor_1 (.a(absB), .b(R), .out(subtractor_1_out));  // open: bin, bout
  Abs abs_2 (.in_1(in_2), .Output_2(sigB), .Output(absB), .in_2(in_3));
  Adder #(.width(32)) adder_1 (.a(divider_1_out), .b(32'h1), .out(adder_1_out));  // open: cin, cout
  Multiplexer #(.width(32)) multiplexer_1 (.in0(R), .in1(subtractor_1_out), .out(Output_2), .sel(negA));  // open: en
  Multiplexer #(.width(32)) multiplexer_2 (
    .in0(divider_1_out), .in1(adder_1_out), .out(multiplexer_2_out), .sel(negA));  // open: en
  Negator #(.width(32)) negator_1 (.in(multiplexer_2_out), .out(negator_1_out));
  Multiplexer #(.width(32)) multiplexer_3 (
    .in0(multiplexer_2_out), .in1(negator_1_out), .out(Output), .sel(negO));  // open: en
  and and_1 (negA, sigA, ~in_3);  // AND_Gate
  and and_2 (negB, ~in_3, sigB);  // AND_Gate
  xor xor_1 (negO, negA, negB);

  // Other names for the same wires on the sheet: A[31:0] = in_1; B[31:0] = in_2; unsigned = in_3
endmodule

module Comparator (
  input  [31:0] in_1,
  input  [31:0] in_2,
  input  in_3,
  output [31:0] Output
);

  wire and_1_out, and_2_out, comparator_1_lt, comparator_2_lt, or_1_out;

  Comparator_part #(.width(32), .mode("unsigned")) comparator_1 (
    .a(in_1), .b(in_2), .lt(comparator_1_lt));  // open: gt, eq
  Comparator_part #(.width(32)) comparator_2 (.a(in_1), .b(in_2), .lt(comparator_2_lt));  // open: gt, eq
  and and_1 (and_1_out, comparator_1_lt, in_3);
  and and_2 (and_2_out, ~in_3, comparator_2_lt);  // AND_Gate
  or or_1 (or_1_out, and_1_out, and_2_out);
  assign Output = {{31{1'b0}}, or_1_out};  // Bit_Extender bit_extender_1

  // Other names for the same wires on the sheet: A[31:0] = in_1; B[31:0] = in_2; unsigned = in_3
endmodule

module DataPath (
  input  [31:0] in_1,
  input  [6:0] in_2,
  input  in_3,
  input  in_4,
  input  in_5,
  input  in_6,
  input  in_7,
  input  in_8,
  input  in_9,
  output out_10,
  output out_11,
  output out_12,
  output out_13,
  output out_14,
  output out_15,
  output out_16,
  output out_17,
  output [31:0] Output,
  output [6:0] TtyData,
  output [31:0] ROut
);

  wire ADD, ADDI, alu_encoder_1_unsigned, AND, ANDI, BEQ, BGTZ, BLEZ, BLTZ, BNE, DIV, DIVU, inmediate, J, JR,
       KBD, LW, MFHI, MFLO, MULT, MULU, NOP, NOR, on, OR, or_1_out, or_8_out, or_9_out, or_10_out, ORI, POP,
       PUSH, RND, SLT, SLTI, SLTIU, SLTU, SUB, SW, XOR, XORI;
  wire [2:0] RFsel;
  wire [3:0] alu_encoder_1_opsel;
  wire [4:0] multiplexer_2_out, RD, RS, RT;
  wire [15:0] Const;
  wire [25:0] JD;
  wire [31:0] branch_control_1_out_13, extKBD, get_instruction_1_out_5, HI, inputRF, LO, PC, random,
       resultALU, RT__star, RT_t, SP;
  wire [31:7] RS_t;
  wire [31:31] and_1_out;

  Get_Instruction get_instruction_1 (
    .in_1(in_3), .in_2(in_1), .in_3(in_4), .out_5(get_instruction_1_out_5), .in_4(in_6));
  or or_1 (or_1_out, SW, ADDI, LW);
  Instruction_Decoder instruction_decoder_1 (
    .Output(NOP), .Output_2(POP), .Output_3(PUSH), .Output_4(KBD), .Output_5(LW), .Output_6(J),
    .Output_7(ADD), .Output_8(SLT), .Output_9(JR), .Output_10(ADDI), .Output_11(SW), .Output_13(SUB),
    .Output_14(SLTU), .Output_15(MFHI), .Output_16(SLTI), .Output_17(BEQ), .in_1(get_instruction_1_out_5),
    .Output_19(MULT), .Output_20(AND), .Output_21(MFLO), .Output_22(SLTIU), .Output_23(BNE),
    .Output_25(MULU), .Output_26(OR), .Output_27(out_10), .Output_28(ANDI), .Output_29(BLEZ),
    .Output_30(DIV), .Output_31(NOR), .Output_32(out_14), .Output_33(XORI), .Output_34(BGTZ),
    .Output_35(DIVU), .Output_36(XOR), .Output_37(RND), .Output_38(ORI), .Output_39(BLTZ), .Output_12(RS),
    .out_42(JD), .out_31(Const), .Output_18(RT), .Output_24(RD));
  Alu_Encoder alu_encoder_1 (
    .in_1(ADD), .in_2(SLT), .in_3(or_1_out), .in_4(SUB), .in_5(SLTU), .in_6(SLTI), .in_7(MULT), .in_8(AND),
    .in_9(SLTIU), .in_10(MULU), .in_11(OR), .in_12(ANDI), .in_13(DIV), .in_14(NOR), .in_15(XORI),
    .in_16(DIVU), .in_17(XOR), .in_18(ORI), .\unsigned (alu_encoder_1_unsigned), .inmediately(inmediate),
    .OpSel(alu_encoder_1_opsel), .Output(on));
  and and_1 (and_1_out[31], ~ANDI, ~ORI, ~XORI, Const[15]);  // AND_Gate
  Multiplexer #(.width(32), .enable("false")) multiplexer_1 (
    .in0(RT_t), .in1({{16{and_1_out[31]}}, Const}), .out(RT__star), .sel(inmediate));
  ALU alu_1 (
    .in_1({RS_t, TtyData}), .in_2(alu_encoder_1_opsel), .Output(LO), .out_8(resultALU), .in_3(in_3),
    .Output_2(HI), .in_4(RT__star), .in_6(alu_encoder_1_unsigned), .in_5(on));
  Register_File register_file_1 (
    .in_1(in_4), .in_2(in_3), .in_3(in_7), .in_4(multiplexer_2_out), .in_5(RS), .Output({RS_t, TtyData}),
    .in_6(inputRF), .Output_2(RT_t), .in_7(RT), .in_8(POP), .in_9(PUSH), .in_10(in_8), .Output_3(SP));
  Multiplexer #(.width(5), .enable("false")) multiplexer_2 (
    .in0(RD), .in1(RT), .out(multiplexer_2_out), .sel(inmediate));
  Branch_Control branch_control_1 (
    .in_1(JD), .in_2({RS_t, TtyData}), .in_3(Const), .in_4(PC), .in_5(RT_t),
    .out_13(branch_control_1_out_13), .in_6(BEQ), .in_7(BLEZ), .in_8(JR), .in_9(BNE), .in_10(BGTZ),
    .in_11(J), .in_12(BLTZ));
  MemAdd memadd_1 (
    .in_1(resultALU), .in_2(POP), .in_3(PUSH), .in_4(LW), .in_5(PC), .in_6(SW), .in_7(in_5), .in_8(SP),
    .Output(Output));
  assign extKBD = {{25{1'b0}}, in_2};  // Bit_Extender bit_extender_1
  Random #(.width(32)) random_1 (.clk(in_3), .next(RND), .out(random));  // open: clr
  or or_2 (RFsel[0], LW, POP, MFLO, KBD);
  or or_3 (RFsel[1], MFLO, MFHI);
  or or_4 (RFsel[2], RND, KBD);
  PC pc_1 (.in_1(in_3), .in_2(in_4), .in_3(in_8), .in_4(branch_control_1_out_13), .Output(PC));
  or or_5 (out_17, PUSH, SW);
  or or_6 (out_16, PUSH, POP);
  or or_7 (out_15, LW, SW);
  or or_8 (or_8_out, XORI, MULT, NOR, MULU, XOR, DIV, ADDI, DIVU);
  Multiplexer #(.select(3), .width(32), .enable("false")) multiplexer_3 (
    .in0(resultALU), .in1(in_1), .in2(HI), .in3(LO), .in4(random), .in5(extKBD), .out(inputRF), .sel(RFsel));  // open: in6, in7
  or or_9 (or_9_out, ADD, AND, ORI, SUB, OR);
  or or_10 (or_10_out, SLTI, SLT, SLTIU, SLTU, ANDI);
  or or_11 (out_12, RND, MFHI, MFLO, KBD, out_14);
  or or_12 (out_13, BGTZ, BEQ, BNE, BLEZ, BLTZ, JR, J, NOP);
  Multiplexer #(.width(32)) multiplexer_4 (.in0({RS_t, TtyData}), .in1(RT_t), .out(ROut), .sel(SW));  // open: en
  or or_13 (out_11, or_9_out, or_8_out, or_10_out);

  // Other names for the same wires on the sheet: Address[31:0] = Output; AluInst = out_11; clk = in_3; enGI = in_6;
  //   enPC = in_8; enRF = in_7; HALT = out_10; Instruction[31:0] = in_1; JmpInst = out_13; kbd_data[6:0] = in_2;
  //   kbdAva = in_9; MemInst = out_15; MemW = in_5; reset = in_4; RInst = out_12; RS_t[6:0] = TtyData;
  //   StackInst = out_16; TTY = out_14; WriteInst = out_17
endmodule

module Alu_Encoder (
  input  in_1,
  input  in_2,
  input  in_3,
  input  in_4,
  input  in_5,
  input  in_6,
  input  in_7,
  input  in_8,
  input  in_9,
  input  in_10,
  input  in_11,
  input  in_12,
  input  in_13,
  input  in_14,
  input  in_15,
  input  in_16,
  input  in_17,
  input  in_18,
  output \unsigned ,
  output inmediately,
  output Output,
  output [3:0] OpSel
);

  wire ADD, AND, MULT, OR, SLT, XOR;

  or or_1 (ADD, in_1, in_3);
  or or_2 (MULT, in_7, in_10);
  or or_3 (OpSel[3], in_13, in_16);
  or or_4 (SLT, in_2, in_5, in_6, in_9);
  or or_5 (AND, in_8, in_12);
  or or_6 (OR, in_11, in_18);
  or or_7 (XOR, in_17, in_15);
  or or_8 (\unsigned , in_10, in_16, in_5, in_9);
  or or_9 (OpSel[0], AND, OpSel[3], ADD, in_14, SLT);
  or or_10 (OpSel[1], in_4, XOR, SLT, OpSel[3], AND);
  or or_11 (OpSel[2], OpSel[3], OR, XOR, SLT);
  or or_12 (inmediately, in_3, in_6, in_9, in_12, in_18, in_15);
  or or_13 (Output, OpSel[0], OpSel[1], OpSel[2], OpSel[3], MULT);

  // Other names for the same wires on the sheet: add_t = in_1; addi = in_3; and_t = in_8; andi = in_12; div_t = in_13;
  //   divu = in_16; mult_t = in_7; mulu = in_10; nor = in_14; _1 = OpSel[0]; _2 = OpSel[1]; _3 = OpSel[2];
  //   DIV = OpSel[3]; or_t = in_11; ori = in_18; slt_t = in_2; slti = in_6; sltiu = in_9; sltu = in_5; sub = in_4;
  //   xor_t = in_17; xori = in_15
endmodule

module Branch_Control (
  input  [25:0] in_1,
  input  [31:0] in_2,
  input  [15:0] in_3,
  input  [31:0] in_4,
  input  [31:0] in_5,
  input  in_6,
  input  in_7,
  input  in_8,
  input  in_9,
  input  in_10,
  input  in_11,
  input  in_12,
  output [31:0] out_13
);

  wire and_1_out, and_2_out, and_3_out, and_4_out, and_5_out, comparator_1_eq, or_3_out, RS___0, RS___0_t,
       RS____0, RS____RT, RS____RT_t;
  wire [1:0] selector;
  wire [31:0] PC___4, PC___4___4_offset;

  Comparator_part #(.width(32)) comparator_1 (.a(in_2), .b({32{1'b0}}), .eq(comparator_1_eq), .lt(RS___0));  // open: gt
  Comparator_part #(.width(32)) comparator_2 (.a(in_2), .b(in_5), .eq(RS____RT_t));  // open: gt, lt
  or or_1 (RS____0, comparator_1_eq, RS___0);
  not not_1 (RS____RT, RS____RT_t);
  Adder #(.width(32)) adder_1 (.a(in_4), .b(32'h4), .out(PC___4));  // open: cin, cout
  not not_2 (RS___0_t, RS____0);
  Adder #(.width(32)) adder_2 (
    .a(PC___4), .b({{15{in_3[15]}}, in_3[14:0], 2'b00}), .out(PC___4___4_offset));  // open: cin, cout
  Multiplexer #(.select(2), .width(32), .enable("false")) multiplexer_1 (
    .in0(PC___4), .in1({in_4[31:28], in_1, 2'b00}), .in2(PC___4___4_offset), .in3(in_2), .out(out_13),
    .sel(selector));
  and and_1 (and_1_out, RS____RT_t, in_6);
  and and_2 (and_2_out, RS____RT, in_9);
  and and_3 (and_3_out, RS____0, in_7);
  and and_4 (and_4_out, RS___0_t, in_10);
  and and_5 (and_5_out, RS___0, in_12);
  or or_2 (selector[0], in_11, in_8);
  or or_3 (or_3_out, and_1_out, and_2_out, and_3_out, and_4_out, and_5_out);
  or or_4 (selector[1], or_3_out, in_8);

  // Other names for the same wires on the sheet: offset[15:0] = in_3; BEQ = in_6; BGTZ = in_10; BLEZ = in_7;
  //   BLTZ = in_12; BNE = in_9; J = in_11; JR = in_8; Destino[25:0] = in_1; JUMP[31:2] = {in_4[31:28], in_1};
  //   PC[31:0] = in_4; OUTPUT[31:0] = out_13; RS[31:0] = in_2; RT[31:0] = in_5
endmodule

module PC (
  input  in_1,
  input  in_2,
  input  in_3,
  input  [31:0] in_4,
  output [31:0] Output
);

  Register #(.width(32)) register_1 (.D(in_4), .en(in_3), .Q(Output), .clk(in_1), .clr(in_2));

  // Other names for the same wires on the sheet: clk = in_1; enable = in_3; reset = in_2
endmodule

module MemAdd (
  input  [31:0] in_1,
  input  in_2,
  input  in_3,
  input  in_4,
  input  [31:0] in_5,
  input  in_6,
  input  in_7,
  input  [31:0] in_8,
  output [31:0] Output
);

  wire [1:0] or_2_out;
  wire [31:0] multiplexer_1_out, subtractor_1_out;

  Multiplexer #(.width(32), .enable("false")) multiplexer_1 (
    .in0(in_8), .in1(subtractor_1_out), .out(multiplexer_1_out), .sel(in_3));
  Subtractor #(.width(32)) subtractor_1 (.a(in_8), .b(32'h4), .out(subtractor_1_out));  // open: bin, bout
  Multiplexer #(.select(2), .width(32), .enable("false")) multiplexer_2 (
    .in0(in_5), .in1(in_1), .in2(multiplexer_1_out), .in3(in_5), .out(Output), .sel(or_2_out));
  or or_1 (or_2_out[1], in_3, in_7, in_2);
  or or_2 (or_2_out[0], in_4, in_7, in_6);

  // Other names for the same wires on the sheet: ALU[31:0] = in_1; enablePC = in_7; lw = in_4; PC[31:0] = in_5;
  //   pop = in_2; push = in_3; SP[31:0] = in_8; sw = in_6
endmodule

module Control_Unit (
  input  in_1,
  input  in_2,
  input  in_3,
  input  in_4,
  input  in_5,
  input  in_6,
  input  in_7,
  input  in_8,
  input  in_9,
  input  in_10,
  input  in_11,
  input  in_12,
  output out_13,
  output out_14,
  output out_15,
  output out_16,
  output out_17,
  output out_18,
  output out_19,
  output out_20,
  output out_21
);

  wire Branch, d_ff_1_q, d_ff_2_q, d_ff_3_q, d_ff_5_q, demultiplexer_1_out0, demultiplexer_1_out1, or_5_out,
       RF;
  wire [2:0] or_1_out;

  D_Flip_Flop #(.trigger("falling")) d_ff_1 (.clk(in_1), .D(in_2), .Q(d_ff_1_q), .reset(in_6));  // open: Qn, preset, en
  or or_1 (or_1_out[0], in_5, in_4, in_11);
  or or_2 (or_1_out[1], in_5, in_9);
  or or_3 (or_1_out[2], in_10, in_11);
  D_Flip_Flop #(.trigger("falling")) d_ff_2 (.clk(in_1), .D(in_3), .Q(d_ff_2_q));  // open: Qn, preset, en, reset
  D_Flip_Flop #(.trigger("falling")) d_ff_3 (
    .clk(in_1), .D(out_14), .Q(d_ff_3_q), .reset(in_6));  // open: Qn, preset, en
  Demultiplexer #(.select(3)) demultiplexer_1 (
    .out0(demultiplexer_1_out0), .out1(demultiplexer_1_out1), .out2(Branch), .out3(RF), .out4(out_16),
    .out5(out_21), .in(d_ff_2_q), .sel(or_1_out));  // open: out6, out7, en
  or or_4 (out_17, d_ff_1_q, d_ff_3_q);
  or or_5 (or_5_out, out_15, demultiplexer_1_out0);
  D_Flip_Flop #(.trigger("falling")) d_ff_4 (
    .clk(in_1), .D(or_5_out), .Q(out_15), .reset(in_6));  // open: Qn, preset, en
  D_Flip_Flop #(.trigger("falling")) d_ff_5 (
    .clk(in_1), .D(demultiplexer_1_out1), .Q(d_ff_5_q), .reset(in_6));  // open: Qn, preset, en
  or or_6 (out_13, d_ff_5_q, in_8, RF);
  D_Flip_Flop #(.trigger("falling")) d_ff_6 (.clk(in_1), .D(out_13), .Q(out_20));  // open: Qn, preset, en, reset
  or or_7 (out_14, out_20, in_12, Branch);
  and and_1 (out_19, out_20, in_7);

  assign out_18 = in_3;

  // Other names for the same wires on the sheet: AluInst = in_4; Clk = in_1; End = out_15; getData = out_16;
  //   getInst = out_17; JmpInst = in_9; MemInst = in_10; ReadyData = in_8; ReadyW = in_12; Reset = in_6; RInst = in_5;
  //   Start = in_2; KbdEn = out_20; Tty = out_20; TtyEn = out_19; TtyInst = in_7; ReadyInst = in_3; useGI = in_3;
  //   Cont = out_14; usePC = out_14; useRF = out_13; Write = out_21; WriteInst = in_11
endmodule

module RAM_Reader (
  input  [31:0] in_1,
  input  [31:0] in_2,
  input  [31:0] in_3,
  input  [31:0] in_4,
  input  [3:0] in_5,
  input  in_6,
  input  in_7,
  input  in_8,
  output [31:0] out_9,
  output [31:0] out_10,
  output [31:0] out_11,
  output [31:0] out_12,
  output out_13,
  output out_14
);

  wire a, or_1_out, Stop, x;

  or or_1 (or_1_out, in_8, Stop);
  D_Flip_Flop #(.trigger("falling")) d_ff_1 (.clk(in_6), .D(in_8), .Q(a), .en(or_1_out));  // open: Qn, preset, reset
  Register #(.width(32)) register_1 (.D(in_1), .en(x), .Q(out_9), .clk(in_6), .clr(in_7));
  Register #(.width(32)) register_2 (.D(in_2), .en(x), .Q(out_10), .clk(in_6), .clr(in_7));
  Timer timer_1 (.in_1(a), .in_2(out_14), .in_3(in_6), .in_4(in_5), .Ready(Stop));
  Register #(.width(32)) register_3 (.D(in_4), .en(x), .Q(out_12), .clk(in_6), .clr(in_7));
  Register #(.width(32)) register_4 (.D(in_3), .en(x), .Q(out_11), .clk(in_6), .clr(in_7));
  D_Flip_Flop #(.trigger("falling")) d_ff_2 (.clk(in_6), .D(Stop), .Q(x), .reset(out_14));  // open: Qn, preset, en
  D_Flip_Flop #(.trigger("falling")) d_ff_3 (.clk(in_6), .D(x), .Q(out_14));  // open: Qn, preset, en, reset
  or or_2 (out_13, x, a);

  // Other names for the same wires on the sheet: Bank0[31:0] = in_1; Bank1[31:0] = in_2; Bank2[31:0] = in_3;
  //   Bank3[31:0] = in_4; BankOut0[31:0] = out_9; BankOut1[31:0] = out_10; BankOut2[31:0] = out_11;
  //   BankOut3[31:0] = out_12; clk = in_6; CS = out_13; get = in_8; ReadTime[3:0] = in_5; ready = out_14;
  //   reset = in_7
endmodule

module RAM_Interaction (
  input  [31:0] in_1,
  input  [31:0] in_2,
  input  [31:0] in_3,
  input  [31:0] in_4,
  input  [31:0] in_5,
  input  [3:0] in_6,
  input  [3:0] in_7,
  input  in_8,
  input  in_9,
  input  in_10,
  input  in_11,
  input  in_12,
  input  in_13,
  output [31:0] out_14,
  output [31:0] out_15,
  output [31:0] out_16,
  output [31:0] out_17,
  output [15:0] out_18,
  output [3:0] out_19,
  output out_20,
  output out_21,
  output out_22,
  output out_23,
  output out_24
);

  wire CSD, CSI, or_1_out, Stop0;
  wire [31:0] DO0, DO1, DO2, DO3, inout_1_output, inout_2_output, inout_3_output, inout_4_output, IO0, IO1,
       IO2, IO3;

  D_Flip_Flop #(.trigger("falling")) d_ff_1 (
    .clk(in_8), .D(in_10), .Q(out_20), .en(or_1_out));  // open: Qn, preset, reset
  or or_1 (or_1_out, in_10, Stop0);
  RAM_Reader ram_reader_1 (
    .in_1(in_1), .in_2(in_2), .in_3(in_3), .in_4(in_4), .in_5(in_6), .in_6(in_8), .in_7(in_9), .in_8(in_11),
    .out_9(IO0), .out_10(IO1), .out_11(IO2), .out_12(IO3), .out_13(CSI), .out_14(out_22));
  Timer timer_1 (.in_1(out_20), .in_2(out_24), .in_3(in_8), .in_4(in_7), .Ready(Stop0));
  D_Flip_Flop #(.trigger("falling")) d_ff_2 (.clk(in_8), .D(Stop0), .Q(out_24));  // open: Qn, preset, en, reset
  RAM_Reader ram_reader_2 (
    .in_1(in_1), .in_2(in_2), .in_3(in_3), .in_4(in_4), .in_5(in_6), .in_6(in_8), .in_7(in_9), .in_8(in_12),
    .out_9(DO0), .out_10(DO1), .out_11(DO2), .out_12(DO3), .out_13(CSD), .out_14(out_23));
  or or_2 (out_21, CSI, out_20, CSD);
  Demultiplexer #(.select(2)) demultiplexer_1 (
    .out0(out_19[0]), .out1(out_19[1]), .out2(out_19[2]), .out3(out_19[3]), .in(1'b1), .sel(in_5[3:2]));  // open: en
  Multiplexer #(.width(32)) multiplexer_1 (.in0(inout_1_output), .in1(IO0), .out(out_14), .sel(in_13));  // open: en
  Multiplexer #(.width(32)) multiplexer_2 (.in0(inout_2_output), .in1(IO2), .out(out_16), .sel(in_13));  // open: en
  InOut inout_1 (.in_1(DO0), .Output(inout_1_output));
  InOut inout_2 (.in_1(DO2), .Output(inout_2_output));
  Multiplexer #(.width(32)) multiplexer_3 (.in0(inout_3_output), .in1(IO1), .out(out_15), .sel(in_13));  // open: en
  Multiplexer #(.width(32)) multiplexer_4 (.in0(inout_4_output), .in1(IO3), .out(out_17), .sel(in_13));  // open: en
  InOut inout_3 (.in_1(DO1), .Output(inout_3_output));
  InOut inout_4 (.in_1(DO3), .Output(inout_4_output));

  assign out_18 = in_5[19:4];

  // Other names for the same wires on the sheet: Bank0[31:0] = in_1; Bank1[31:0] = in_2; Bank2[31:0] = in_3;
  //   Bank3[31:0] = in_4; BankOut0[31:0] = out_14; BankOut1[31:0] = out_15; BankOut2[31:0] = out_16;
  //   BankOut3[31:0] = out_17; clk = in_8; CS = out_21; DPAddress[31:0] = in_5; ADDR[15:0] = in_5[19:4];
  //   getData = in_12; getInst = in_11; isInst = in_13; MASK[3:0] = out_19; ReadTime[3:0] = in_6; ReadyData = out_23;
  //   ReadyInst = out_22; ReadyWrite = out_24; reset = in_9; RW = out_20; Write = in_10; WriteTime[3:0] = in_7
endmodule

module Timer (
  input  in_1,
  input  in_2,
  input  in_3,
  input  [3:0] in_4,
  output Ready
);

  wire [3:0] counter_1_q;

  Counter #(.width(4), .max('hf)) counter_1 (
    .count(in_1), .Q(counter_1_q), .clk(in_3), .clr(in_2));  // open: load, D, carry
  Comparator_part #(.width(4)) comparator_1 (.a(in_4), .b(counter_1_q), .eq(Ready));  // open: gt, lt

  // Other names for the same wires on the sheet: Clk = in_3; Reset = in_2; Start = in_1; Time[3:0] = in_4
endmodule

module InOut (
  input  [31:0] in_1,
  output [31:0] Output
);


  assign Output = {in_1[7:0], in_1[15:8], in_1[23:16], in_1[31:24]};
endmodule
